// Logisim project 8.circ as structural Verilog: 3 circuits, main circuit A
module A (
  input  A,
  input  B,
  output Diff,
  output Borrow
);

  wire and_2_out, not_1_out, not_2_out;

  not not_1 (not_1_out, A);
  and and_1 (Borrow, not_1_out, B);
  not not_2 (not_2_out, B);
  and and_2 (and_2_out, not_2_out, A);
  or or_1 (Diff, Borrow, and_2_out);
endmodule

module B (
  input  A,
  input  B,
  input  Borrow,
  output Diff,
  output Borrow_2
);

  wire a_1_borrow, a_1_diff, a_2_borrow, nand_1_out, nand_2_out;

  A a_1 (.A(A), .B(B), .Diff(a_1_diff), .Borrow(a_1_borrow));
  nand nand_1 (nand_1_out, a_1_borrow, a_1_borrow);
  A a_2 (.A(a_1_diff), .B(Borrow), .Diff(Diff), .Borrow(a_2_borrow));
  nand nand_2 (nand_2_out, a_2_borrow, a_2_borrow);
  nand nand_3 (Borrow_2, nand_2_out, nand_1_out);
endmodule

module C (
  input  X0,
  input  Y0,
  input  X1,
  input  Y1,
  input  X2,
  input  Y2,
  input  X3,
  input  Y3,
  output d1,
  output d2,
  output d3,
  output d4
);

  wire a_1_borrow, a_1_diff, b_1_borrow_2, b_1_diff, b_2_borrow_2, b_2_diff, b_3_borrow_2, b_3_diff,
       not_1_out;

  A a_1 (.A(X0), .B(Y0), .Diff(a_1_diff), .Borrow(a_1_borrow));
  B b_1 (.A(X1), .B(Y1), .Borrow(a_1_borrow), .Diff(b_1_diff), .Borrow_2(b_1_borrow_2));
  B b_2 (.A(X2), .B(Y2), .Borrow(b_1_borrow_2), .Diff(b_2_diff), .Borrow_2(b_2_borrow_2));
  B b_3 (.A(X3), .B(Y3), .Borrow(b_2_borrow_2), .Diff(b_3_diff), .Borrow_2(b_3_borrow_2));
  not not_1 (not_1_out, b_3_borrow_2);
  and and_1 (d1, a_1_diff, not_1_out);
  and and_2 (d2, b_1_diff, not_1_out);
  and and_3 (d3, b_2_diff, not_1_out);
  and and_4 (d4, b_3_diff, not_1_out);
endmodule
