// Logisim project 9.circ as structural Verilog: 1 circuit, main circuit main
module main (
  input  X1,
  input  Y1,
  input  X0,
  input  Y0,
  output out_5
);

  wire and_1_out, and_2_out, and_3_out, not_1_out, not_2_out, or_1_out;

  not not_1 (not_1_out, Y1);
  not not_2 (not_2_out, Y0);
  and and_1 (and_1_out, X1, not_1_out);
  or or_1 (or_1_out, X1, not_1_out);
  and and_2 (and_2_out, X0, not_2_out);
  and and_3 (and_3_out, or_1_out, and_2_out);
  or or_2 (out_5, and_1_out, and_3_out);
endmodule
